# Fritzing sketch buzzer (saved by Fritzing 0.9.3b)

parts:
  Part1 = Arduino Uno (Rev3)
  J1 = Generic female header - 3 pins [form="♀ (female)" package=THT]

nets:
  N1: Part1.D8, J1.IO
  GND: Part1.GND, J1.GND

notes:
  File > Examples > Digital > ToneMelody
  Can you compose something?

custom parts:
  Generic female header - 3 pins: Generic female header
