# Fritzing sketch fade (saved by Fritzing 0.9.3b)

parts:
  Part1 = Arduino Uno (Rev3)
  J1 = Generic female header - 4 pins [form="♀ (female)" package=THT]

nets:
  N1: Part1.D9_PWM, J1.R
  GND: Part1.GND, J1.GND

notes:
  File > Examples > Basics > Fade
  RED LED should slowly go on and off.
  How do you change color?
  Can you change the frequency?
  RGB LED

custom parts:
  Generic female header - 4 pins: Generic female header
