# Fritzing sketch BME280 (saved by Fritzing 0.9.3b)

parts:
  Part1 = Arduino Uno (Rev3)
  J2 = Generic female header - 6 pins [form="♀ (female)" package=THT]

nets:
  N1: Part1.A4/SDA, J2.pin4
  N2: Part1.A5/SCL, J2.pin3
  N3: Part1.3V3, J2.pin1
  N4: Part1.GND, J2.pin2

notes:
  1. In Arduino IDE -> Sketch -> Include Library -> Manage Libraries
  2. Type in BME
  3. Select and install Adafruit BME280 library by Adafruit
  4. In Arduino IDE -> Sketch -> Include Library -> Manage Libraries
  5. Type in Adafruit Unified Sensor
  6. Select and install Adafruit Unified Sensor library by Adafruit
  7. In Arduino IDE -> File -> Examples -> Adafruit BME280 Library -> BME280 Test
  8. Change bme.begin() to bme.begin(0x76)
  9. Load
  10. In Arduino IDE -> Tools -> Serial Monitor
  BME280
  3.3v not 5v !

custom parts:
  Generic female header - 6 pins: Generic female header
