# Fritzing sketch OLED (saved by Fritzing 0.9.3b)

parts:
  Part2 = Arduino Uno (Rev3)
  J1 = Generic female header - 4 pins [form="♀ (female)" package=THT]

nets:
  N1: Part2.A4/SDA, J1.pin4
  N2: Part2.A5/SCL, J1.pin3
  N3: Part2.5V, J1.pin2
  N4: Part2.GND, J1.pin1

notes:
  1. Sketch > Include Library > Manage Libraries
  2. Type in Adafruit SSD1306
  3. Select the choice and install
  4. Sketch > Include Library > Manage Libraries
  5. Type in Adafruit GFX
  6. Select the choice and install
  7. File > Examples > Adafruit SSD1306 > ssd1306_128x64_i2c
  8. Change 3D to 3C on this line: display.begin(SSD1306_SWITCHCAPVCC, 0x3D)
  9. Upload the code

custom parts:
  Generic female header - 4 pins: Generic female header
