# Fritzing sketch pulse_sensor (saved by Fritzing 0.9.3b)

parts:
  Part1 = Arduino Uno (Rev3)
  J2 = Generic female header - 3 pins [form="♀ (female)" package=THT]

nets:
  N1: Part1.A0, J2.signal
  5V: Part1.5V, J2.VSS
  GND: Part1.GND, J2.GND

notes:
  brown
  red
  orange
  5v GND A0
  1. Go https://github.com/WorldFamousElectronics/PulseSensorPlayground
  2. click "Clone or download"
  3. click "Download ZIP" (remember where it gets downloaded)
  4. In Arduino IDE -> Sketch -> Include Library -> Add .ZIP library
  5. Give it the dounloaded ZIP
  6. In Arduino IDE -> File -> Examples -> PulseSensor Playground -> GettingStartedProject
  7. In Arduino IDE -> Tools -> Serial Plotter (you should see a heart beat plot)
  8. In Arduino IDE -> File -> Examples -> PulseSensor Playground -> Getting_BMP_to_Monitor
  9. In Arduino IDE -> Tools -> Serial Monitor

custom parts:
  Generic female header - 3 pins: Generic female header
