# Fritzing sketch pump (saved by Fritzing 0.9.3b)

parts:
  J2 = Generic female header - 8 pins [form="♀ (female)" package=THT]  # not connected
  J5 = Generic female header - 2 pins [form="♀ (female)" package=THT]
  J6 = Generic female header - 2 pins [form="♀ (female)" package=THT]

nets:
  N1: J5.pin1, J6.pin_5

notes:
  0. Disconnect Arduino from USB
  Make connections:
  1. Black from pump -> GND
  2. Red from pump -> COM om relay
  3. NO (normally open) on relay -> VIN
  4. VCC on relay -> RED on Arduino
  5. GND on relay -> BLACK on Arduino
  6. IN on relay -> 13 on Arduino
  7. Load Blink from examples.
  8. Change interval to 5 seconds.

custom parts:
  Generic female header - 8 pins: Generic female header
  Generic female header - 2 pins: Generic female header
  Generic female header - 2 pins: Generic female header
